// Logisim project ALU.circ as structural Verilog: 1 circuit, main circuit ALU
module ALU (
  input  [19:0] I0,
  input  [19:0] I1,
  input  [2:0] OP_Select,
  input  BE_Select,
  output C_out,
  output [19:0] S,
  output E
);

  wire multiplexer_1_out, n20_bit_adder_1_o, n20bitsubtractor_1_b_out, nor_1_out;
  wire [19:0] n20_bit_adder_1_s, n20bitbitwiseand_1_s, n20bitbitwiseor_1_r, n20bitbitwisexor_1_s,
       n20bitsubtractor_1_d;

  nor nor_1 (nor_1_out, OP_Select[2], OP_Select[1]);
  _20_Bit_Adder u_20_bit_adder_1 (.N0(I0), .N1(I1), .S(n20_bit_adder_1_s), .O(n20_bit_adder_1_o));
  _20BitSubtractor u_20bitsubtractor_1 (.I0(I0), .B_out(n20bitsubtractor_1_b_out), .D(n20bitsubtractor_1_d), .I1(I1));
  _20BitBitwiseAnd u_20bitbitwiseand_1 (.I0(I0), .I1(I1), .S(n20bitbitwiseand_1_s));
  _20BitBitwiseOr u_20bitbitwiseor_1 (.N0(I0), .N1(I1), .R(n20bitbitwiseor_1_r));
  _20BitBitwiseXor u_20bitbitwisexor_1 (.I0(I0), .I1(I1), .S(n20bitbitwisexor_1_s));
  EqualityComparator equalitycomparator_1 (.I0(I0), .I1(I1), .BE_Select(BE_Select), .S(E));
  and and_1 (C_out, nor_1_out, multiplexer_1_out);
  Multiplexer #(.disabled(0), .enable("false")) multiplexer_1 (
    .in0(n20_bit_adder_1_o), .in1(n20bitsubtractor_1_b_out), .out(multiplexer_1_out), .sel(OP_Select[0]));
  Multiplexer #(.select(3), .width(20), .disabled(0), .enable("false")) multiplexer_2 (
    .in0(n20_bit_adder_1_s), .in1(n20bitsubtractor_1_d), .in2(n20bitbitwiseand_1_s),
    .in3(n20bitbitwiseor_1_r), .in4(n20bitbitwisexor_1_s), .out(S), .sel(OP_Select));  // open: in5, in6, in7

  // Notes on the sheet:
  //   OP_Select: pull=down
  //   S: pull=down
  //   I0: pull=down
  //   BE_Select: pull=down
  //   I1: pull=down
  //   E: pull=down
  //   C_out: pull=down
endmodule
