// Logisim project 20BitAdder.circ as structural Verilog: 1 circuit, main circuit 20 Bit Adder
module _20_Bit_Adder (
  input  [19:0] I0,
  input  [19:0] I1,
  output [19:0] S,
  output C_out
);

  wire full_adder_1_c_out, full_adder_2_c_out, full_adder_3_c_out, full_adder_4_c_out, full_adder_5_c_out,
       full_adder_6_c_out, full_adder_7_c_out, full_adder_8_c_out, full_adder_9_c_out, full_adder_10_c_out,
       full_adder_11_c_out, full_adder_12_c_out, full_adder_13_c_out, full_adder_14_c_out,
       full_adder_15_c_out, full_adder_16_c_out, full_adder_17_c_out, full_adder_18_c_out, half_adder_1_c_out;

  Half_Adder half_adder_1 (.I0(I0[0]), .I1(I1[0]), .S(S[0]), .C_out(half_adder_1_c_out));
  Full_Adder full_adder_1 (.C_in(half_adder_1_c_out), .I0(I0[1]), .I1(I1[1]), .S(S[1]), .C_out(full_adder_1_c_out));
  Full_Adder full_adder_2 (.C_in(full_adder_1_c_out), .I0(I0[2]), .I1(I1[2]), .S(S[2]), .C_out(full_adder_2_c_out));
  Full_Adder full_adder_3 (.C_in(full_adder_2_c_out), .I0(I0[3]), .I1(I1[3]), .S(S[3]), .C_out(full_adder_3_c_out));
  Full_Adder full_adder_4 (.C_in(full_adder_3_c_out), .I0(I0[4]), .I1(I1[4]), .S(S[4]), .C_out(full_adder_4_c_out));
  Full_Adder full_adder_5 (.C_in(full_adder_4_c_out), .I0(I0[5]), .I1(I1[5]), .S(S[5]), .C_out(full_adder_5_c_out));
  Full_Adder full_adder_6 (.C_in(full_adder_5_c_out), .I0(I0[6]), .I1(I1[6]), .S(S[6]), .C_out(full_adder_6_c_out));
  Full_Adder full_adder_7 (.C_in(full_adder_6_c_out), .I0(I0[7]), .I1(I1[7]), .S(S[7]), .C_out(full_adder_7_c_out));
  Full_Adder full_adder_8 (.C_in(full_adder_7_c_out), .I0(I0[8]), .I1(I1[8]), .S(S[8]), .C_out(full_adder_8_c_out));
  Full_Adder full_adder_9 (.C_in(full_adder_8_c_out), .I0(I0[9]), .I1(I1[9]), .S(S[9]), .C_out(full_adder_9_c_out));
  Full_Adder full_adder_10 (
    .C_in(full_adder_9_c_out), .I0(I0[10]), .I1(I1[10]), .S(S[10]), .C_out(full_adder_10_c_out));
  Full_Adder full_adder_11 (
    .C_in(full_adder_10_c_out), .I0(I0[11]), .I1(I1[11]), .S(S[11]), .C_out(full_adder_11_c_out));
  Full_Adder full_adder_12 (
    .C_in(full_adder_11_c_out), .I0(I0[12]), .I1(I1[12]), .S(S[12]), .C_out(full_adder_12_c_out));
  Full_Adder full_adder_13 (
    .C_in(full_adder_12_c_out), .I0(I0[13]), .I1(I1[13]), .S(S[13]), .C_out(full_adder_13_c_out));
  Full_Adder full_adder_14 (
    .C_in(full_adder_13_c_out), .I0(I0[14]), .I1(I1[14]), .S(S[14]), .C_out(full_adder_14_c_out));
  Full_Adder full_adder_15 (
    .C_in(full_adder_14_c_out), .I0(I0[15]), .I1(I1[15]), .S(S[15]), .C_out(full_adder_15_c_out));
  Full_Adder full_adder_16 (
    .C_in(full_adder_15_c_out), .I0(I0[16]), .I1(I1[16]), .S(S[16]), .C_out(full_adder_16_c_out));
  Full_Adder full_adder_17 (
    .C_in(full_adder_16_c_out), .I0(I0[17]), .I1(I1[17]), .S(S[17]), .C_out(full_adder_17_c_out));
  Full_Adder full_adder_18 (
    .C_in(full_adder_17_c_out), .I0(I0[18]), .I1(I1[18]), .S(S[18]), .C_out(full_adder_18_c_out));
  Full_Adder full_adder_19 (.C_in(full_adder_18_c_out), .I0(I0[19]), .I1(I1[19]), .S(S[19]), .C_out(C_out));

  // Notes on the sheet:
  //   I0: pull=down
  //   I1: pull=down
  //   S: pull=down
endmodule
