// Logisim project FullAdder.circ as structural Verilog: 1 circuit, main circuit Full Adder
module Full_Adder (
  input  C_in,
  input  I0,
  input  I1,
  output S,
  output C_out
);

  wire half_adder_1_c, half_adder_1_s, half_adder_2_c;

  Half_Adder half_adder_1 (.A(I0), .B(I1), .S(half_adder_1_s), .C(half_adder_1_c));
  Half_Adder half_adder_2 (.A(C_in), .B(half_adder_1_s), .S(S), .C(half_adder_2_c));
  or or_1 (C_out, half_adder_2_c, half_adder_1_c);

  // Notes on the sheet:
  //   I0: pull=down
  //   I1: pull=down
  //   S: pull=down
  //   C_out: pull=down
  //   C_in: pull=down
endmodule
