// Logisim project HalfAdder.circ as structural Verilog: 1 circuit, main circuit Half Adder
module Half_Adder (
  input  I0,
  input  I1,
  output S,
  output C_out
);

  xor xor_1 (S, I0, I1);
  and and_1 (C_out, I0, I1);

  // Notes on the sheet:
  //   S: pull=down
  //   I0: pull=down
  //   C_out: pull=down
  //   I1: pull=down
endmodule
