// Logisim project 10BitIncrementer.circ as structural Verilog: 1 circuit, main circuit 10BitIncrementer
module _10BitIncrementer (
  input  [9:0] I,
  output [9:0] S,
  output Overflow
);

  wire half_adder_1_c, half_adder_2_c, half_adder_3_c, half_adder_4_c, half_adder_5_c, half_adder_6_c,
       half_adder_7_c, half_adder_8_c, half_adder_9_c;

  Half_Adder half_adder_1 (.A(1'b1), .B(I[0]), .S(S[0]), .C(half_adder_1_c));
  Half_Adder half_adder_2 (.A(half_adder_1_c), .B(I[1]), .S(S[1]), .C(half_adder_2_c));
  Half_Adder half_adder_3 (.A(half_adder_2_c), .B(I[2]), .S(S[2]), .C(half_adder_3_c));
  Half_Adder half_adder_4 (.A(half_adder_3_c), .B(I[3]), .S(S[3]), .C(half_adder_4_c));
  Half_Adder half_adder_5 (.A(half_adder_4_c), .B(I[4]), .S(S[4]), .C(half_adder_5_c));
  Half_Adder half_adder_6 (.A(half_adder_5_c), .B(I[5]), .S(S[5]), .C(half_adder_6_c));
  Half_Adder half_adder_7 (.A(half_adder_6_c), .B(I[6]), .S(S[6]), .C(half_adder_7_c));
  Half_Adder half_adder_8 (.A(half_adder_7_c), .B(I[7]), .S(S[7]), .C(half_adder_8_c));
  Half_Adder half_adder_9 (.A(half_adder_8_c), .B(I[8]), .S(S[8]), .C(half_adder_9_c));
  Half_Adder half_adder_10 (.A(half_adder_9_c), .B(I[9]), .S(S[9]), .C(Overflow));

  // Notes on the sheet:
  //   Overflow: pull=down
  //   S: pull=down
  //   I: pull=down
endmodule
