// Logisim project 20BitIncrementer.circ as structural Verilog: 1 circuit, main circuit 20BitIncrementer
module _20BitIncrementer (
  input  [19:0] I,
  output [19:0] O
);

  wire half_adder_1_c_out, half_adder_2_c_out, half_adder_3_c_out, half_adder_4_c_out, half_adder_5_c_out,
       half_adder_6_c_out, half_adder_7_c_out, half_adder_8_c_out, half_adder_9_c_out, half_adder_10_c_out,
       half_adder_11_c_out, half_adder_12_c_out, half_adder_13_c_out, half_adder_14_c_out,
       half_adder_15_c_out, half_adder_16_c_out, half_adder_17_c_out, half_adder_18_c_out,
       half_adder_19_c_out;

  Half_Adder half_adder_1 (.I0(1'b1), .I1(I[0]), .S(O[0]), .C_out(half_adder_1_c_out));
  Half_Adder half_adder_2 (.I0(half_adder_1_c_out), .I1(I[1]), .S(O[1]), .C_out(half_adder_2_c_out));
  Half_Adder half_adder_3 (.I0(half_adder_2_c_out), .I1(I[2]), .S(O[2]), .C_out(half_adder_3_c_out));
  Half_Adder half_adder_4 (.I0(half_adder_3_c_out), .I1(I[3]), .S(O[3]), .C_out(half_adder_4_c_out));
  Half_Adder half_adder_5 (.I0(half_adder_4_c_out), .I1(I[4]), .S(O[4]), .C_out(half_adder_5_c_out));
  Half_Adder half_adder_6 (.I0(half_adder_5_c_out), .I1(I[5]), .S(O[5]), .C_out(half_adder_6_c_out));
  Half_Adder half_adder_7 (.I0(half_adder_6_c_out), .I1(I[6]), .S(O[6]), .C_out(half_adder_7_c_out));
  Half_Adder half_adder_8 (.I0(half_adder_7_c_out), .I1(I[7]), .S(O[7]), .C_out(half_adder_8_c_out));
  Half_Adder half_adder_9 (.I0(half_adder_8_c_out), .I1(I[8]), .S(O[8]), .C_out(half_adder_9_c_out));
  Half_Adder half_adder_10 (.I0(half_adder_9_c_out), .I1(I[9]), .S(O[9]), .C_out(half_adder_10_c_out));
  Half_Adder half_adder_11 (.I0(half_adder_10_c_out), .I1(I[10]), .S(O[10]), .C_out(half_adder_11_c_out));
  Half_Adder half_adder_12 (.I0(half_adder_11_c_out), .I1(I[11]), .S(O[11]), .C_out(half_adder_12_c_out));
  Half_Adder half_adder_13 (.I0(half_adder_12_c_out), .I1(I[12]), .S(O[12]), .C_out(half_adder_13_c_out));
  Half_Adder half_adder_14 (.I0(half_adder_13_c_out), .I1(I[13]), .S(O[13]), .C_out(half_adder_14_c_out));
  Half_Adder half_adder_15 (.I0(half_adder_14_c_out), .I1(I[14]), .S(O[14]), .C_out(half_adder_15_c_out));
  Half_Adder half_adder_16 (.I0(half_adder_15_c_out), .I1(I[15]), .S(O[15]), .C_out(half_adder_16_c_out));
  Half_Adder half_adder_17 (.I0(half_adder_16_c_out), .I1(I[16]), .S(O[16]), .C_out(half_adder_17_c_out));
  Half_Adder half_adder_18 (.I0(half_adder_17_c_out), .I1(I[17]), .S(O[17]), .C_out(half_adder_18_c_out));
  Half_Adder half_adder_19 (.I0(half_adder_18_c_out), .I1(I[18]), .S(O[18]), .C_out(half_adder_19_c_out));
  Half_Adder half_adder_20 (.I0(half_adder_19_c_out), .I1(I[19]), .S(O[19]));  // open: C_out

  // Notes on the sheet:
  //   I: pull=down
  //   O: pull=down
endmodule
