// Logisim project 20BitBitwiseAnd.circ as structural Verilog: 1 circuit, main circuit 20BitBitwiseAnd
module _20BitBitwiseAnd (
  input  [19:0] I0,
  input  [19:0] I1,
  output [19:0] S
);

  and and_1 (S[0], I0[0], I1[0]);
  and and_2 (S[19], I0[19], I1[19]);
  and and_3 (S[1], I0[1], I1[1]);
  and and_4 (S[2], I0[2], I1[2]);
  and and_5 (S[18], I0[18], I1[18]);
  and and_6 (S[17], I0[17], I1[17]);
  and and_7 (S[4], I0[4], I1[4]);
  and and_8 (S[3], I0[3], I1[3]);
  and and_9 (S[16], I0[16], I1[16]);
  and and_10 (S[15], I0[15], I1[15]);
  and and_11 (S[5], I0[5], I1[5]);
  and and_12 (S[6], I0[6], I1[6]);
  and and_13 (S[14], I0[14], I1[14]);
  and and_14 (S[13], I0[13], I1[13]);
  and and_15 (S[7], I0[7], I1[7]);
  and and_16 (S[8], I0[8], I1[8]);
  and and_17 (S[12], I0[12], I1[12]);
  and and_18 (S[11], I0[11], I1[11]);
  and and_19 (S[9], I0[9], I1[9]);
  and and_20 (S[10], I0[10], I1[10]);

  // Notes on the sheet:
  //   I0: pull=down
  //   I1: pull=down
  //   S: pull=down
endmodule
