// Logisim project BitwiseAnd.circ as structural Verilog: 1 circuit, main circuit BitwiseAnd
module BitwiseAnd (
  input  [19:0] N0,
  input  [19:0] N1,
  output [19:0] S
);

  and and_1 (S[0], N0[0], N1[0]);
  and and_2 (S[19], N0[19], N1[19]);
  and and_3 (S[2], N0[2], N1[2]);
  and and_4 (S[1], N0[1], N1[1]);
  and and_5 (S[18], N0[18], N1[18]);
  and and_6 (S[17], N0[17], N1[17]);
  and and_7 (S[4], N0[4], N1[4]);
  and and_8 (S[3], N0[3], N1[3]);
  and and_9 (S[16], N0[16], N1[16]);
  and and_10 (S[15], N0[15], N1[15]);
  and and_11 (S[6], N0[6], N1[6]);
  and and_12 (S[5], N0[5], N1[5]);
  and and_13 (S[14], N0[14], N1[14]);
  and and_14 (S[13], N0[13], N1[13]);
  and and_15 (S[7], N0[7], N1[7]);
  and and_16 (S[8], N0[8], N1[8]);
  and and_17 (S[12], N0[12], N1[12]);
  and and_18 (S[11], N0[11], N1[11]);
  and and_19 (S[9], N0[9], N1[9]);
  and and_20 (S[10], N0[10], N1[10]);
endmodule
