// Logisim project 20BitBitwiseOr.circ as structural Verilog: 1 circuit, main circuit 20BitBitwiseOr
module _20BitBitwiseOr (
  input  [19:0] N0,
  input  [19:0] N1,
  output [19:0] R
);

  or or_1 (R[0], N0[0], N1[0]);
  or or_2 (R[19], N0[19], N1[19]);
  or or_3 (R[1], N0[1], N1[1]);
  or or_4 (R[2], N0[2], N1[2]);
  or or_5 (R[18], N0[18], N1[18]);
  or or_6 (R[17], N0[17], N1[17]);
  or or_7 (R[3], N0[3], N1[3]);
  or or_8 (R[4], N0[4], N1[4]);
  or or_9 (R[15], N0[15], N1[15]);
  or or_10 (R[16], N0[16], N1[16]);
  or or_11 (R[5], N0[5], N1[5]);
  or or_12 (R[6], N0[6], N1[6]);
  or or_13 (R[14], N0[14], N1[14]);
  or or_14 (R[13], N0[13], N1[13]);
  or or_15 (R[8], N0[8], N1[8]);
  or or_16 (R[7], N0[7], N1[7]);
  or or_17 (R[11], N0[11], N1[11]);
  or or_18 (R[12], N0[12], N1[12]);
  or or_19 (R[9], N0[9], N1[9]);
  or or_20 (R[10], N0[10], N1[10]);

  // Notes on the sheet:
  //   R: pull=down
  //   N1: pull=down
  //   N0: pull=down
endmodule
