// Logisim project 20BitBitwiseXor.circ as structural Verilog: 1 circuit, main circuit 20BitBitwiseXor
module _20BitBitwiseXor (
  input  [19:0] I0,
  input  [19:0] I1,
  output [19:0] S
);

  xor xor_1 (S[0], I0[0], I1[0]);
  xor xor_2 (S[19], I0[19], I1[19]);
  xor xor_3 (S[1], I0[1], I1[1]);
  xor xor_4 (S[2], I0[2], I1[2]);
  xor xor_5 (S[18], I0[18], I1[18]);
  xor xor_6 (S[17], I0[17], I1[17]);
  xor xor_7 (S[3], I0[3], I1[3]);
  xor xor_8 (S[4], I0[4], I1[4]);
  xor xor_9 (S[15], I0[15], I1[15]);
  xor xor_10 (S[16], I0[16], I1[16]);
  xor xor_11 (S[6], I0[6], I1[6]);
  xor xor_12 (S[5], I0[5], I1[5]);
  xor xor_13 (S[13], I0[13], I1[13]);
  xor xor_14 (S[14], I0[14], I1[14]);
  xor xor_15 (S[7], I0[7], I1[7]);
  xor xor_16 (S[8], I0[8], I1[8]);
  xor xor_17 (S[11], I0[11], I1[11]);
  xor xor_18 (S[12], I0[12], I1[12]);
  xor xor_19 (S[9], I0[9], I1[9]);
  xor xor_20 (S[10], I0[10], I1[10]);

  // Notes on the sheet:
  //   I0: pull=down
  //   S: pull=down
  //   I1: pull=down
endmodule
