// Logisim project CPU.circ as structural Verilog: 1 circuit, main circuit CPU
module CPU (
);

  wire ALU_Control, and_1_out, and_2_out, BE_Select, BEQ, clk, Cout, Fetch, Imm, MemRead, MemWrite, or_1_out,
       PC_Overflow, PCRead, PCW_Select, PCWrite, RegRead, RegW_Select, RegWrite, zero;
  wire [2:0] ALU_Select;
  wire [3:0] Dr, Sr1, Sr2;
  wire [9:0] Addr, multiplexer_1_out, multiplexer_4_out, PC;
  wire [19:0] ALQ, ALUQ, bit_extender_1_out, Imm_Offset, MemQ, multiplexer_2_out, multiplexer_3_out,
       multiplexer_5_out, R1, R2;

  Multiplexer #(.width(10), .disabled(0), .enable("false")) multiplexer_1 (
    .in0(Addr), .in1(PC), .out(multiplexer_1_out), .sel(Fetch));
  Multiplexer #(.width(20), .disabled(0), .enable("false")) multiplexer_2 (
    .in0(R1), .in1(bit_extender_1_out), .out(multiplexer_2_out), .sel(PCRead));
  assign bit_extender_1_out = {{10{1'b0}}, PC};  // Bit_Extender bit_extender_1
  Multiplexer #(.width(20), .disabled(0), .enable("false")) multiplexer_3 (
    .in0(R2), .in1(Imm_Offset), .out(multiplexer_3_out), .sel(Imm));
  and and_1 (and_1_out, PCW_Select, BEQ);
  Memory memory_1 (.clk(clk), .Mem_Select(Fetch), .WR_Select(MemWrite), .A(multiplexer_1_out), .D(R1), .D_2(MemQ));
  Multiplexer #(.width(10), .disabled(0), .enable("false")) multiplexer_4 (
    .in0(ALQ[9:0]), .in1(Addr), .out(multiplexer_4_out), .sel(and_1_out));
  ALU alu_1 (
    .I0(multiplexer_2_out), .I1(multiplexer_3_out), .OP_Select(ALU_Select), .BE_Select(BE_Select), .S(ALQ),
    .E(BEQ), .C_out(Cout));
  ProgramCounter programcounter_1 (
    .Addr(multiplexer_4_out), .Fetch(Fetch), .PCWrite(PCWrite), .clk(clk), .t_0(zero),
    .PC_Overflow(PC_Overflow), .PC(PC));
  Clock clock_1 (.clk(clk), .t_0(zero));
  or or_1 (or_1_out, PC_Overflow, and_2_out);
  Control_Unit Control_Unit (
    .PC_Overflow(or_1_out), .Inst(MemQ), .clk(clk), .t_0(zero), .Fetch(Fetch), .ALU_Control(ALU_Control),
    .RegRead(RegRead), .RegWrite(RegWrite), .MemRead(MemRead), .MemWrite(MemWrite), .PCRead(PCRead),
    .PCWrite(PCWrite), .Imm(Imm), .PCW_Select(PCW_Select), .BE_Select(BE_Select), .ALU_Select(ALU_Select),
    .Dr(Dr), .Sr1(Sr1), .Sr2(Sr2), .Imm_Offset(Imm_Offset), .Addr(Addr), .PCR_Select(RegW_Select));  // open: RegW_Select
  and and_2 (and_2_out, PCRead, Cout);
  Multiplexer #(.width(20), .disabled(0), .enable("false")) multiplexer_5 (
    .in0(MemQ), .in1(ALUQ), .out(multiplexer_5_out), .sel(RegW_Select));
  RegisterFile registerfile_1 (
    .W_Enabled(RegWrite), .W_Select(Dr), .W(multiplexer_5_out), .R1_Select(Sr1), .R2_Select(Sr2), .R2(R2),
    .R1(R1), .clk(clk), .reset(zero));
endmodule
