// Logisim project Clock.circ as structural Verilog: 1 circuit, main circuit Clock
module Clock (
  output clk,
  output t_0
);

  Clock_part clock_1 (.out(clk));
  TickOnceAtZero tickonceatzero_1 (.clk(clk), .Tick(t_0));

  // Notes on the sheet:
  //   clk: pull=down
  //   t_0: pull=down
endmodule
