// Logisim project ProgramCounter.circ as structural Verilog: 1 circuit, main circuit ProgramCounter
module ProgramCounter (
  input  [9:0] Addr,
  input  Fetch,
  input  PCWrite,
  input  clk,
  input  t_0,
  output PC_Overflow,
  output [9:0] PC
);

  wire or_1_out;
  wire [9:0] multiplexer_1_out, n10bitincrementer_1_s;

  or or_1 (or_1_out, Fetch, PCWrite);
  Multiplexer #(.width(10), .disabled(0), .enable("false")) multiplexer_1 (
    .in0(Addr), .in1(n10bitincrementer_1_s), .out(multiplexer_1_out), .sel(Fetch));
  _10BitRegister u_10bitregister_1 (.clk(clk), .W_Enable(or_1_out), .I(multiplexer_1_out), .Q(PC), .reset(t_0));
  _10BitIncrementer u_10bitincrementer_1 (.I(PC), .S(n10bitincrementer_1_s), .Overflow(PC_Overflow));

  // Notes on the sheet:
  //   Addr: pull=down
  //   Fetch: pull=down
  //   t_0: pull=down
  //   clk: pull=down
  //   PC_Overflow: pull=down
  //   PCWrite: pull=down
  //   PC: pull=down
endmodule
