// Logisim project ControlUnit.circ as structural Verilog: 4 circuits, main circuit Control Unit
module Control_Unit (
  input  clk,
  input  Halt,
  input  [19:0] Ins,
  output Fetch,
  output ALU_Control,
  output RegRead,
  output RegWrite,
  output PCRead,
  output PCWrite,
  output MemWrite,
  output MemRead,
  output BE_Select,
  output [2:0] ALU_Select,
  output [3:0] DR,
  output [3:0] SR1,
  output [3:0] SR2,
  output [19:0] Imm_Offset,
  output [9:0] Addr,
  output Imm
);

  wire and_1_out, and_2_out, and_3_out, and_4_out, and_5_out, and_6_out, and_7_out, and_8_out, Halt_q,
       instruction_decoder_1_alu, instruction_decoder_1_be, instruction_decoder_1_halt,
       instruction_decoder_1_jump, instruction_decoder_1_ld, instruction_decoder_1_pop,
       instruction_decoder_1_push, instruction_decoder_1_st, nor_1_out, not_1_out, not_2_out, or_1_out,
       or_2_out, or_3_out, or_4_out, or_5_out, or_6_out, or_7_out, state_manager_1_s0, state_manager_1_s1;

  or or_1 (or_1_out, Halt, instruction_decoder_1_halt);
  RisingEdgeTriggeredDFlipFlop u_Halt (.D(or_1_out), .C(clk), .Q(Halt_q), .E(or_1_out));
  Instruction_Decoder instruction_decoder_1 (
    .in_1(Ins), .ALU_Select(ALU_Select), .ALU(instruction_decoder_1_alu), .IMM(Imm),
    .LD(instruction_decoder_1_ld), .ST(instruction_decoder_1_st), .PUSH(instruction_decoder_1_push),
    .POP(instruction_decoder_1_pop), .JUMP(instruction_decoder_1_jump), .BE(instruction_decoder_1_be),
    .BE_Select(BE_Select), .HALT(instruction_decoder_1_halt), .DR(DR), .SR1(SR1), .SR2(SR2),
    .IMM_2(Imm_Offset), .ADDR(Addr));
  nor nor_1 (nor_1_out, Halt_q, or_1_out);
  State_Manager state_manager_1 (
    .ALU(instruction_decoder_1_alu), .LD(instruction_decoder_1_ld), .ST(instruction_decoder_1_st),
    .PUSH(instruction_decoder_1_push), .POP(instruction_decoder_1_pop), .JUMP(instruction_decoder_1_jump),
    .BE(instruction_decoder_1_be), .clk(clk), .S1(state_manager_1_s1), .S0(state_manager_1_s0));
  not not_1 (not_1_out, state_manager_1_s1);
  not not_2 (not_2_out, state_manager_1_s0);
  or or_2 (or_2_out, instruction_decoder_1_alu, instruction_decoder_1_jump, instruction_decoder_1_be);
  or or_3 (or_3_out, instruction_decoder_1_alu, instruction_decoder_1_st, instruction_decoder_1_push, instruction_decoder_1_be);
  or or_4 (or_4_out, instruction_decoder_1_alu, instruction_decoder_1_ld, instruction_decoder_1_pop);
  and and_1 (and_1_out, not_2_out, not_1_out);
  and and_2 (and_2_out, state_manager_1_s1, not_2_out, or_2_out);
  or or_5 (or_5_out, instruction_decoder_1_be, instruction_decoder_1_jump);
  or or_6 (or_6_out, instruction_decoder_1_push, instruction_decoder_1_st);
  or or_7 (or_7_out, instruction_decoder_1_pop, instruction_decoder_1_ld);
  and and_3 (and_3_out, state_manager_1_s0, not_1_out, or_3_out);
  and and_4 (and_4_out, state_manager_1_s0, state_manager_1_s1, or_4_out);
  and and_5 (and_5_out, state_manager_1_s0, state_manager_1_s1, or_6_out);
  and and_6 (and_6_out, state_manager_1_s0, not_1_out, or_7_out);
  and and_7 (and_7_out, state_manager_1_s0, not_1_out, instruction_decoder_1_jump);
  and and_8 (and_8_out, state_manager_1_s0, state_manager_1_s1, or_5_out);
  and and_9 (Fetch, nor_1_out, and_1_out);
  and and_10 (ALU_Control, nor_1_out, and_2_out);
  and and_11 (RegRead, nor_1_out, and_3_out);
  and and_12 (RegWrite, nor_1_out, and_4_out);
  and and_13 (PCRead, nor_1_out, and_7_out);
  and and_14 (PCWrite, nor_1_out, and_8_out);
  and and_15 (MemWrite, nor_1_out, and_5_out);
  and and_16 (MemRead, nor_1_out, and_6_out);

  // Notes on the sheet:
  //   Imm: pull=down
  //   ALU_Select: pull=down
  //   Addr: pull=down
  //   Imm_Offset: pull=down
  //   Halt: pull=down
  //   RegRead: pull=down
  //   MemRead: pull=down
  //   PCRead: pull=down
  //   RegWrite: pull=down
  //   ALU_Control: pull=down
  //   SR1: pull=down
  //   MemWrite: pull=down
  //   BE_Select: pull=down
  //   clk: pull=down
  //   Fetch: pull=down
  //   DR: pull=down
  //   PCWrite: pull=down
  //   Ins: pull=down
  //   SR2: pull=down
endmodule

module Instruction_Decoder (
  input  [19:0] in_1,
  output [2:0] ALU_Select,
  output ALU,
  output IMM,
  output LD,
  output ST,
  output PUSH,
  output POP,
  output JUMP,
  output BE,
  output BE_Select,
  output HALT,
  output [3:0] DR,
  output [3:0] SR1,
  output [3:0] SR2,
  output [19:0] IMM_2,
  output [9:0] ADDR
);

  wire decoder_1_out1, decoder_1_out2, decoder_1_out3, decoder_1_out4, decoder_1_out5, decoder_1_out6,
       decoder_1_out7, decoder_1_out8, decoder_1_out9, decoder_1_out10, decoder_1_out17, or_1_out, or_4_out,
       or_5_out, or_7_out;
  wire [0:0] or_12_out;
  wire [1:0] or_10_out;
  wire [9:0] bit_extender_2_out;

  or or_1 (or_1_out, decoder_1_out3, decoder_1_out4);
  or or_2 (ALU_Select[0], or_1_out, or_5_out);
  or or_3 (ALU_Select[1], or_4_out, or_5_out);
  or or_4 (or_4_out, decoder_1_out5, decoder_1_out6);
  or or_5 (or_5_out, decoder_1_out7, decoder_1_out8);
  or or_6 (ALU_Select[2], decoder_1_out9, decoder_1_out10);
  Decoder #(.select(5), .disabled(0), .enable("false")) decoder_1 (
    .out0(HALT), .out1(decoder_1_out1), .out2(decoder_1_out2), .out3(decoder_1_out3), .out4(decoder_1_out4),
    .out5(decoder_1_out5), .out6(decoder_1_out6), .out7(decoder_1_out7), .out8(decoder_1_out8),
    .out9(decoder_1_out9), .out10(decoder_1_out10), .out11(LD), .out12(ST), .out13(PUSH), .out14(POP),
    .out15(JUMP), .out16(BE_Select), .out17(decoder_1_out17), .sel(in_1[19:15]));  // open: out18, out19, out20, out21, out22, out23, out24, out25, out26, out27, out28, out29, out30, out31
  assign IMM_2 = {{13{in_1[6]}}, in_1[6:0]};  // Bit_Extender bit_extender_1
  assign bit_extender_2_out = {{3{1'b0}}, in_1[6:0]};  // Bit_Extender bit_extender_2
  Multiplexer #(.select(2), .width(4), .disabled(0), .enable("false")) multiplexer_1 (
    .in0(in_1[14:11]), .in1(in_1[13:10]), .in2(in_1[11:8]), .in3(in_1[3:0]), .out(DR), .sel(or_10_out));
  Multiplexer #(.select(3), .width(4), .disabled(0), .enable("false")) multiplexer_2 (
    .in0(in_1[14:11]), .in1(in_1[13:10]), .in2(in_1[10:7]), .in3(in_1[7:4]), .in4(in_1[3:0]), .out(SR1),
    .sel({PUSH, ALU, or_12_out[0]}));  // open: in5, in6, in7
  Multiplexer #(.width(4), .enable("false")) multiplexer_3 (
    .in0(in_1[10:7]), .in1(in_1[3:0]), .out(SR2), .sel(or_7_out));
  Multiplexer #(.width(10), .disabled(0), .enable("false")) multiplexer_4 (
    .in0(in_1[9:0]), .in1(bit_extender_2_out), .out(ADDR), .sel(BE));
  or or_7 (or_7_out, decoder_1_out9, decoder_1_out7, decoder_1_out5, decoder_1_out3, decoder_1_out1);
  or or_8 (IMM, decoder_1_out2, decoder_1_out4, decoder_1_out6, decoder_1_out8, decoder_1_out10);
  or or_9 (BE, BE_Select, decoder_1_out17);
  or or_10 (or_10_out[0], LD, POP);
  or or_11 (or_10_out[1], or_7_out, POP);
  or or_12 (or_12_out[0], or_7_out, ST);
  or or_13 (ALU, or_7_out, IMM);

  // Notes on the sheet:
  //   ALU: pull=down
  //   IMM: pull=down
  //   JUMP: pull=down
  //   ADDR: pull=down
  //   DR: pull=down
  //   POP: pull=down
  //   SR1: pull=down
  //   SR2: pull=down
  //   IMM_2: pull=down
  //   HALT: pull=down
  //   in_1: pull=down
  //   PUSH: pull=down
  //   ST: pull=down
  //   LD: pull=down
  //   BE: pull=down
  //   BE_Select: pull=down
  //   ALU_Select: pull=down
endmodule

module Next_State (
  input  ALU,
  input  LD,
  input  ST,
  input  PUSH,
  input  POP,
  input  JUMP,
  input  BE,
  input  S1,
  input  S0,
  output S1_,
  output S0_
);

  wire and_1_out, and_2_out, and_3_out, and_4_out, and_5_out, and_6_out, and_7_out, not_1_out, not_2_out,
       not_3_out, not_4_out, not_5_out, not_6_out, not_7_out, not_8_out, or_1_out, or_2_out;

  not not_1 (not_1_out, S1);
  not not_2 (not_2_out, S0);
  not not_3 (not_3_out, S0);
  not not_4 (not_4_out, S0);
  not not_5 (not_5_out, S1);
  not not_6 (not_6_out, S0);
  not not_7 (not_7_out, S1);
  or or_1 (or_1_out, LD, ST, PUSH, POP);
  not not_8 (not_8_out, S0);
  or or_2 (or_2_out, ALU, JUMP, BE);
  and and_1 (and_1_out, not_1_out, S0);
  and and_2 (and_2_out, BE, S1, not_2_out);
  and and_3 (and_3_out, JUMP, S1, not_3_out);
  and and_4 (and_4_out, ALU, S1, not_4_out);
  and and_5 (and_5_out, not_5_out, not_6_out);
  and and_6 (and_6_out, not_7_out, S0, or_1_out);
  and and_7 (and_7_out, S1, not_8_out, or_2_out);
  or or_3 (S1_, and_1_out, and_2_out, and_3_out, and_4_out);
  or or_4 (S0_, and_5_out, and_6_out, and_7_out);

  // Notes on the sheet:
  //   S0: pull=down
  //   S1: pull=down
  //   LD: pull=down
  //   BE: pull=down
  //   ALU: pull=down
  //   PUSH: pull=down
  //   S0_: pull=down
  //   POP: pull=down
  //   JUMP: pull=down
  //   ST: pull=down
  //   S1_: pull=down
endmodule

module State_Manager (
  input  ALU,
  input  LD,
  input  ST,
  input  PUSH,
  input  POP,
  input  JUMP,
  input  BE,
  input  clk,
  output S1,
  output S0
);

  wire next_state_1_s0_, next_state_1_s1_;

  RisingEdgeTriggeredDFlipFlop u_S1 (.D(next_state_1_s1_), .C(clk), .Q(S1), .E(1'b1));
  RisingEdgeTriggeredDFlipFlop u_S0 (.D(next_state_1_s0_), .C(clk), .Q(S0), .E(1'b1));
  Next_State next_state_1 (
    .ALU(ALU), .LD(LD), .ST(ST), .PUSH(PUSH), .POP(POP), .JUMP(JUMP), .BE(BE), .S1(S1), .S0(S0),
    .S1_(next_state_1_s1_), .S0_(next_state_1_s0_));

  // Notes on the sheet:
  //   ALU: pull=down
  //   PUSH: pull=down
  //   ST: pull=down
  //   LD: pull=down
  //   S1: pull=down
  //   POP: pull=down
  //   S0: pull=down
  //   clk: pull=down
  //   BE: pull=down
  //   JUMP: pull=down
  //   State 10 : Execute
  //   State 00 : Fetch & Decode
  //   State 01 : Fetch Operands
  //   State 11 : Store Results
endmodule
