// Logisim project InstructionDecoder.circ as structural Verilog: 1 circuit, main circuit Instruction Decoder
module Instruction_Decoder (
  input  [19:0] in_1,
  output [2:0] ALU_Select,
  output ALU,
  output IMM,
  output LD,
  output ST,
  output PUSH,
  output POP,
  output JUMP,
  output BE,
  output BE_Select,
  output HALT,
  output [3:0] DR,
  output [3:0] SR1,
  output [3:0] SR2,
  output [19:0] IMM_2,
  output [9:0] ADDR
);

  wire decoder_1_out1, decoder_1_out2, decoder_1_out3, decoder_1_out4, decoder_1_out5, decoder_1_out6,
       decoder_1_out7, decoder_1_out8, decoder_1_out9, decoder_1_out10, decoder_1_out17, or_1_out, or_4_out,
       or_5_out, or_7_out, or_8_out;
  wire [0:0] or_12_out;
  wire [1:0] or_10_out;
  wire [9:0] bit_extender_2_out;

  or or_1 (or_1_out, decoder_1_out3, decoder_1_out4);
  or or_2 (ALU_Select[1], or_4_out, or_5_out);
  or or_3 (ALU_Select[0], or_1_out, or_5_out);
  or or_4 (or_4_out, decoder_1_out5, decoder_1_out6);
  or or_5 (or_5_out, decoder_1_out7, decoder_1_out8);
  or or_6 (ALU_Select[2], decoder_1_out9, decoder_1_out10);
  Decoder #(.select(5), .disabled(0), .enable("false")) decoder_1 (
    .out0(HALT), .out1(decoder_1_out1), .out2(decoder_1_out2), .out3(decoder_1_out3), .out4(decoder_1_out4),
    .out5(decoder_1_out5), .out6(decoder_1_out6), .out7(decoder_1_out7), .out8(decoder_1_out8),
    .out9(decoder_1_out9), .out10(decoder_1_out10), .out11(LD), .out12(ST), .out13(PUSH), .out14(POP),
    .out15(JUMP), .out16(BE_Select), .out17(decoder_1_out17), .sel(in_1[19:15]));  // open: out18, out19, out20, out21, out22, out23, out24, out25, out26, out27, out28, out29, out30, out31
  assign IMM_2 = {{13{in_1[6]}}, in_1[6:0]};  // Bit_Extender bit_extender_1
  assign bit_extender_2_out = {{3{1'b0}}, in_1[6:0]};  // Bit_Extender bit_extender_2
  Multiplexer #(.select(2), .width(4), .disabled(0), .enable("false")) multiplexer_1 (
    .in0(in_1[14:11]), .in1(in_1[13:10]), .in2(in_1[11:8]), .in3(in_1[3:0]), .out(DR), .sel(or_10_out));
  Multiplexer #(.select(3), .width(4), .disabled(0), .enable("false")) multiplexer_2 (
    .in0(in_1[14:11]), .in1(in_1[13:10]), .in2(in_1[10:7]), .in3(in_1[7:4]), .in4(in_1[3:0]), .out(SR1),
    .sel({PUSH, ALU, or_12_out[0]}));  // open: in5, in6, in7
  Multiplexer #(.width(4), .enable("false")) multiplexer_3 (
    .in0(in_1[10:7]), .in1(in_1[3:0]), .out(SR2), .sel(or_7_out));
  Multiplexer #(.width(10), .disabled(0), .enable("false")) multiplexer_4 (
    .in0(in_1[9:0]), .in1(bit_extender_2_out), .out(ADDR), .sel(BE));
  or or_7 (or_7_out, decoder_1_out9, decoder_1_out7, decoder_1_out5, decoder_1_out3, decoder_1_out1);
  or or_8 (or_8_out, decoder_1_out2, decoder_1_out4, decoder_1_out6, decoder_1_out8, decoder_1_out10);
  or or_9 (BE, BE_Select, decoder_1_out17);
  or or_10 (or_10_out[0], LD, POP);
  or or_11 (or_10_out[1], or_7_out, POP);
  or or_12 (or_12_out[0], or_7_out, ST);
  or or_13 (ALU, or_7_out, or_8_out);
  or or_14 (IMM, or_8_out, JUMP);

  // Notes on the sheet:
  //   SR2: pull=down
  //   BE_Select: pull=down
  //   DR: pull=down
  //   BE: pull=down
  //   ALU_Select: pull=down
  //   IMM_2: pull=down
  //   ADDR: pull=down
  //   HALT: pull=down
  //   ST: pull=down
  //   ALU: pull=down
  //   in_1: pull=down
  //   PUSH: pull=down
  //   LD: pull=down
  //   JUMP: pull=down
  //   SR1: pull=down
  //   POP: pull=down
  //   IMM: pull=down
endmodule
