// Logisim project NextState.circ as structural Verilog: 1 circuit, main circuit Next State
module Next_State (
  input  ALU,
  input  LD,
  input  ST,
  input  PUSH,
  input  POP,
  input  JUMP,
  input  BE,
  input  S2,
  input  S1,
  input  S0,
  output S2_,
  output S1_,
  output S0_
);

  wire and_1_out, and_2_out, and_3_out, and_4_out, not_1_out, not_2_out, not_3_out, not_4_out, not_5_out,
       not_6_out, not_7_out, not_8_out, or_1_out, or_2_out, or_3_out, or_4_out, or_5_out, or_6_out;

  not not_1 (not_1_out, S0);
  or or_1 (or_1_out, LD, ST, PUSH, POP);
  not not_2 (not_2_out, S1);
  not not_3 (not_3_out, S0);
  or or_2 (or_2_out, ALU, JUMP, BE);
  or or_3 (or_3_out, ALU, JUMP, BE);
  and and_1 (and_1_out, not_1_out, or_1_out);
  and and_2 (and_2_out, not_2_out, S0);
  and and_3 (and_3_out, not_3_out, S1, or_2_out);
  not not_4 (not_4_out, S1);
  and and_4 (and_4_out, S1, or_3_out);
  not not_5 (not_5_out, S2);
  or or_4 (or_4_out, S0, and_1_out);
  not not_6 (not_6_out, S2);
  or or_5 (or_5_out, and_2_out, and_3_out);
  not not_7 (not_7_out, S2);
  not not_8 (not_8_out, S0);
  or or_6 (or_6_out, not_4_out, and_4_out);
  and and_5 (S2_, not_5_out, S1, or_4_out);
  and and_6 (S1_, not_6_out, or_5_out);
  and and_7 (S0_, not_7_out, not_8_out, or_6_out);

  // Notes on the sheet:
  //   PUSH: pull=down
  //   BE: pull=down
  //   S1_: pull=down
  //   S0_: pull=down
  //   S0: pull=down
  //   S2: pull=down
  //   ALU: pull=down
  //   POP: pull=down
  //   LD: pull=down
  //   ST: pull=down
  //   S1: pull=down
  //   JUMP: pull=down
  //   S2_: pull=down
endmodule
