// Logisim project SignalGenerator.circ as structural Verilog: 1 circuit, main circuit Signal Generator
module Signal_Generator (
  input  HALTED,
  input  ALU,
  input  LD,
  input  ST,
  input  PUSH,
  input  POP,
  input  JUMP,
  input  BE,
  input  S2,
  input  S1,
  input  S0,
  output InstructionEnd,
  output Fetch,
  output Decode,
  output ALUControl,
  output RegRead,
  output RegWrite,
  output MemRead,
  output MemWrite,
  output PCRead,
  output PCWrite,
  output Push_2,
  output Pop_2
);

  wire not_1_out, not_2_out, not_3_out, not_4_out, not_5_out, not_6_out, not_7_out, not_8_out, not_9_out,
       not_10_out, not_11_out, not_12_out, not_13_out, not_14_out, not_15_out, not_16_out, not_17_out,
       not_18_out, not_19_out, not_20_out, not_21_out, not_22_out, not_23_out, not_24_out, not_25_out,
       not_26_out, not_27_out, not_28_out, not_29_out, not_30_out, not_31_out, not_32_out, not_33_out,
       not_34_out, not_35_out, not_36_out, or_1_out, or_2_out, or_3_out, or_4_out, or_5_out;

  not not_1 (not_1_out, S1);
  not not_2 (not_2_out, S0);
  not not_3 (not_3_out, HALTED);
  not not_4 (not_4_out, S2);
  not not_5 (not_5_out, S1);
  not not_6 (not_6_out, S0);
  not not_7 (not_7_out, HALTED);
  not not_8 (not_8_out, S2);
  not not_9 (not_9_out, S1);
  not not_10 (not_10_out, HALTED);
  not not_11 (not_11_out, S2);
  not not_12 (not_12_out, HALTED);
  not not_13 (not_13_out, S2);
  not not_14 (not_14_out, S0);
  or or_1 (or_1_out, ALU, ST, PUSH, BE);
  not not_15 (not_15_out, HALTED);
  not not_16 (not_16_out, S1);
  not not_17 (not_17_out, S0);
  or or_2 (or_2_out, ALU, LD, POP);
  not not_18 (not_18_out, HALTED);
  not not_19 (not_19_out, S2);
  not not_20 (not_20_out, S0);
  or or_3 (or_3_out, LD, POP);
  not not_21 (not_21_out, HALTED);
  not not_22 (not_22_out, S1);
  not not_23 (not_23_out, S0);
  or or_4 (or_4_out, ST, PUSH);
  not not_24 (not_24_out, HALTED);
  not not_25 (not_25_out, S2);
  not not_26 (not_26_out, S0);
  not not_27 (not_27_out, HALTED);
  not not_28 (not_28_out, S1);
  not not_29 (not_29_out, S0);
  or or_5 (or_5_out, JUMP, BE);
  not not_30 (not_30_out, HALTED);
  not not_31 (not_31_out, S1);
  not not_32 (not_32_out, S0);
  not not_33 (not_33_out, HALTED);
  not not_34 (not_34_out, S2);
  not not_35 (not_35_out, S0);
  not not_36 (not_36_out, HALTED);
  and and_1 (InstructionEnd, S2, not_1_out, not_2_out, not_3_out);
  and and_2 (Fetch, not_4_out, not_5_out, not_6_out, not_7_out);
  and and_3 (Decode, not_8_out, not_9_out, S0, not_10_out);
  and and_4 (ALUControl, not_11_out, S1, S0, not_12_out);
  and and_5 (RegRead, not_13_out, S1, not_14_out, or_1_out, not_15_out);
  and and_6 (RegWrite, S2, not_16_out, not_17_out, or_2_out, not_18_out);
  and and_7 (MemRead, not_19_out, S1, not_20_out, or_3_out, not_21_out);
  and and_8 (MemWrite, S2, not_22_out, not_23_out, or_4_out, not_24_out);
  and and_9 (PCRead, not_25_out, S1, not_26_out, JUMP, not_27_out);
  and and_10 (PCWrite, S2, not_28_out, not_29_out, or_5_out, not_30_out);
  and and_11 (Push_2, S2, not_31_out, not_32_out, PUSH, not_33_out);
  and and_12 (Pop_2, not_34_out, S1, not_35_out, POP, not_36_out);

  // Notes on the sheet:
  //   Push_2: pull=down
  //   MemRead: pull=down
  //   PUSH: pull=down
  //   S1: pull=down
  //   ALU: pull=down
  //   POP: pull=down
  //   BE: pull=down
  //   LD: pull=down
  //   JUMP: pull=down
  //   ALUControl: pull=down
  //   S0: pull=down
  //   ST: pull=down
  //   Pop_2: pull=down
  //   HALTED: pull=down
  //   Fetch: pull=down
  //   PCRead: pull=down
  //   S2: pull=down
  //   Decode: pull=down
  //   PCWrite: pull=down
  //   MemWrite: pull=down
  //   RegWrite: pull=down
  //   RegRead: pull=down
  //   InstructionEnd: pull=down
endmodule
