// Logisim project StackPointer.circ as structural Verilog: 1 circuit, main circuit Stack Pointer
module Stack_Pointer (
  input  clk,
  input  Pop,
  input  Push,
  output [9:0] SP,
  output StackAddress,
  output Stack_Overflow
);

  wire n10bitdecrementer_1_overflow, n10bitincrementer_1_overflow, tickonceatzero_1_tick;
  wire [9:0] multiplexer_1_out, multiplexer_2_out, n10bitdecrementer_1_s, n10bitincrementer_1_s;

  TickOnceAtZero tickonceatzero_1 (.clk(clk), .Tick(tickonceatzero_1_tick));
  or or_1 (StackAddress, tickonceatzero_1_tick, Pop, Push);
  Multiplexer #(.width(10), .disabled(0), .enable("false")) multiplexer_1 (
    .in0(multiplexer_2_out), .in1({10{1'b1}}), .out(multiplexer_1_out), .sel(tickonceatzero_1_tick));
  _10BitRegister u_10bitregister_1 (.C(StackAddress), .E(clk), .I(multiplexer_1_out), .Q(SP));
  _10BitIncrementer u_10bitincrementer_1 (.I(SP), .S(n10bitincrementer_1_s), .Overflow(n10bitincrementer_1_overflow));
  _10BitDecrementer u_10bitdecrementer_1 (.I(SP), .S(n10bitdecrementer_1_s), .Overflow(n10bitdecrementer_1_overflow));
  Multiplexer #(.width(10), .disabled(0), .enable("false")) multiplexer_2 (
    .in0(n10bitincrementer_1_s), .in1(n10bitdecrementer_1_s), .out(multiplexer_2_out), .sel(Push));
  Multiplexer #(.disabled(0)) multiplexer_3 (
    .in0(n10bitincrementer_1_overflow), .in1(n10bitdecrementer_1_overflow), .out(Stack_Overflow), .sel(Push),
    .en(StackAddress));

  // Notes on the sheet:
  //   Push: pull=down
  //   Stack_Overflow: pull=down
  //   SP: pull=down
  //   StackAddress: pull=down
  //   Pop: pull=down
  //   clk: pull=down
endmodule
