// Logisim project StateManager.circ as structural Verilog: 1 circuit, main circuit State Manager
module State_Manager (
  input  ALU,
  input  LD,
  input  ST,
  input  PUSH,
  input  POP,
  input  JUMP,
  input  BE,
  input  clk,
  output S2,
  output S1,
  output S0
);

  wire next_state_1_s0_, next_state_1_s1_, next_state_1_s2_;

  RisingEdgeTriggeredDFlipFlop u_S2 (.D(next_state_1_s2_), .clk(clk), .Q(S2), .W_Enable(1'b1));
  RisingEdgeTriggeredDFlipFlop u_S1 (.D(next_state_1_s1_), .clk(clk), .Q(S1), .W_Enable(1'b1));
  RisingEdgeTriggeredDFlipFlop u_S0 (.D(next_state_1_s0_), .clk(clk), .Q(S0), .W_Enable(1'b1));
  Next_State next_state_1 (
    .ALU(ALU), .LD(LD), .ST(ST), .PUSH(PUSH), .POP(POP), .JUMP(JUMP), .BE(BE), .S2(S2), .S1(S1), .S0(S0),
    .S2_(next_state_1_s2_), .S1_(next_state_1_s1_), .S0_(next_state_1_s0_));

  // Notes on the sheet:
  //   S2: pull=down
  //   PUSH: pull=down
  //   ALU: pull=down
  //   POP: pull=down
  //   S0: pull=down
  //   S1: pull=down
  //   ST: pull=down
  //   BE: pull=down
  //   LD: pull=down
  //   JUMP: pull=down
  //   clk: pull=down
endmodule
