// Logisim project EqualityChecker.circ as structural Verilog: 1 circuit, main circuit EqualityChecker
module EqualityChecker (
  input  [19:0] N0,
  input  [19:0] N1,
  input  S,
  output R
);

  wire not_1_out, or_1_out;
  wire [19:0] n20bitbitwisexor_1_s;

  not not_1 (not_1_out, S);
  _20BitBitwiseXor u_20bitbitwisexor_1 (.I0(N0), .I1(N1), .S(n20bitbitwisexor_1_s));
  or or_1 (or_1_out, n20bitbitwisexor_1_s[0], n20bitbitwisexor_1_s[1], n20bitbitwisexor_1_s[2], n20bitbitwisexor_1_s[3], n20bitbitwisexor_1_s[4], n20bitbitwisexor_1_s[5], n20bitbitwisexor_1_s[6], n20bitbitwisexor_1_s[7], n20bitbitwisexor_1_s[8], n20bitbitwisexor_1_s[9], n20bitbitwisexor_1_s[10], n20bitbitwisexor_1_s[11], n20bitbitwisexor_1_s[12], n20bitbitwisexor_1_s[13], n20bitbitwisexor_1_s[14], n20bitbitwisexor_1_s[15], n20bitbitwisexor_1_s[16], n20bitbitwisexor_1_s[17], n20bitbitwisexor_1_s[18], n20bitbitwisexor_1_s[19]);
  xnor xnor_1 (R, or_1_out, not_1_out);

  // Notes on the sheet:
  //   R: pull=down
  //   S: pull=down
  //   N1: pull=down
  //   N0: pull=down
endmodule
