// Logisim project EqualityComparator.circ as structural Verilog: 1 circuit, main circuit EqualityComparator
module EqualityComparator (
  input  [19:0] I0,
  input  [19:0] I1,
  input  BE_Select,
  output S
);

  wire not_1_out, or_1_out;
  wire [19:0] n20bitbitwisexor_1_r;

  not not_1 (not_1_out, BE_Select);
  _20BitBitwiseXor u_20bitbitwisexor_1 (.N0(I0), .N1(I1), .R(n20bitbitwisexor_1_r));
  or or_1 (or_1_out, n20bitbitwisexor_1_r[0], n20bitbitwisexor_1_r[1], n20bitbitwisexor_1_r[2], n20bitbitwisexor_1_r[3], n20bitbitwisexor_1_r[4], n20bitbitwisexor_1_r[5], n20bitbitwisexor_1_r[6], n20bitbitwisexor_1_r[7], n20bitbitwisexor_1_r[8], n20bitbitwisexor_1_r[9], n20bitbitwisexor_1_r[10], n20bitbitwisexor_1_r[11], n20bitbitwisexor_1_r[12], n20bitbitwisexor_1_r[13], n20bitbitwisexor_1_r[14], n20bitbitwisexor_1_r[15], n20bitbitwisexor_1_r[16], n20bitbitwisexor_1_r[17], n20bitbitwisexor_1_r[18], n20bitbitwisexor_1_r[19]);
  xnor xnor_1 (S, or_1_out, not_1_out);

  // Notes on the sheet:
  //   I0: pull=down
  //   BE_Select: pull=down
  //   S: pull=down
  //   I1: pull=down
endmodule
