// Logisim project DLatch.circ as structural Verilog: 1 circuit, main circuit DLatch
module DLatch (
  input  D,
  input  clk,
  input  clr,
  output Q
);

  wire nand_1_out, nand_2_out, nand_4_out, nor_1_out, not_1_out, not_2_out;

  not not_1 (not_1_out, D);
  nand nand_1 (nand_1_out, D, clk);
  nand nand_2 (nand_2_out, clk, not_1_out);
  not not_2 (not_2_out, nand_2_out);
  nor nor_1 (nor_1_out, not_2_out, clr);
  nand nand_3 (Q, nand_1_out, nand_4_out);
  nand nand_4 (nand_4_out, Q, nor_1_out);

  // Notes on the sheet:
  //   clk: pull=down
  //   clr: pull=down
  //   Q: pull=down
  //   D: pull=down
endmodule
