// Logisim project RisingEdgeTriggeredDFlipFlop.circ as structural Verilog: 1 circuit, main circuit RisingEdgeTriggeredDFlipFlop
module RisingEdgeTriggeredDFlipFlop (
  input  D,
  input  W_Enable,
  input  clk,
  output Q
);

  wire dlatch_1_q, multiplexer_1_out, not_1_out, tickonceatzero_1_tick;

  Multiplexer #(.enable("false")) multiplexer_1 (.in0(Q), .in1(D), .out(multiplexer_1_out), .sel(W_Enable));
  not not_1 (not_1_out, clk);
  TickOnceAtZero tickonceatzero_1 (.clk(clk), .Tick(tickonceatzero_1_tick));
  DLatch dlatch_1 (.D(multiplexer_1_out), .clk(not_1_out), .Q(dlatch_1_q), .clr(1'b0));
  DLatch dlatch_2 (.D(dlatch_1_q), .clk(clk), .Q(Q), .clr(tickonceatzero_1_tick));

  // Notes on the sheet:
  //   Q: pull=down
  //   D: pull=down
  //   clk: pull=down
  //   W_Enable: pull=down
endmodule
