// Logisim project TickOnceAtZero.circ as structural Verilog: 1 circuit, main circuit TickOnceAtZero
module TickOnceAtZero (
  input  clk,
  output Tick
);

  wire and_1_out, fallingedgetriggereddflipflop_1_q, half_adder_1_c, half_adder_1_s, not_1_out;

  not not_1 (not_1_out, clk);
  and and_1 (and_1_out, not_1_out, Tick);
  FallingEdgeTriggeredDFlipFlop fallingedgetriggereddflipflop_1 (
    .D(half_adder_1_s), .clk(and_1_out), .Q(fallingedgetriggereddflipflop_1_q), .W_Enable(1'b1));
  Half_Adder half_adder_1 (.A(fallingedgetriggereddflipflop_1_q), .B(1'b1), .S(half_adder_1_s), .C(half_adder_1_c));
  nor nor_1 (Tick, fallingedgetriggereddflipflop_1_q, half_adder_1_c);

  // Notes on the sheet:
  //   clk: pull=down
endmodule
