// Logisim project 10BitRegister.circ as structural Verilog: 1 circuit, main circuit 10BitRegister
module _10BitRegister (
  input  [9:0] I,
  input  clk,
  input  W_Enable,
  input  reset,
  output [9:0] Q
);

  RisingEdgeTriggeredDFlipFlop risingedgetriggereddflipflop_1 (
    .D(I[9]), .clk(clk), .Q(Q[9]), .W_Enable(W_Enable), .reset(reset));
  RisingEdgeTriggeredDFlipFlop risingedgetriggereddflipflop_2 (
    .D(I[8]), .clk(clk), .Q(Q[8]), .W_Enable(W_Enable), .reset(reset));
  RisingEdgeTriggeredDFlipFlop risingedgetriggereddflipflop_3 (
    .D(I[7]), .clk(clk), .Q(Q[7]), .W_Enable(W_Enable), .reset(reset));
  RisingEdgeTriggeredDFlipFlop risingedgetriggereddflipflop_4 (
    .D(I[6]), .clk(clk), .Q(Q[6]), .W_Enable(W_Enable), .reset(reset));
  RisingEdgeTriggeredDFlipFlop risingedgetriggereddflipflop_5 (
    .D(I[5]), .clk(clk), .Q(Q[5]), .W_Enable(W_Enable), .reset(reset));
  RisingEdgeTriggeredDFlipFlop risingedgetriggereddflipflop_6 (
    .D(I[4]), .clk(clk), .Q(Q[4]), .W_Enable(W_Enable), .reset(reset));
  RisingEdgeTriggeredDFlipFlop risingedgetriggereddflipflop_7 (
    .D(I[3]), .clk(clk), .Q(Q[3]), .W_Enable(W_Enable), .reset(reset));
  RisingEdgeTriggeredDFlipFlop risingedgetriggereddflipflop_8 (
    .D(I[2]), .clk(clk), .Q(Q[2]), .W_Enable(W_Enable), .reset(reset));
  RisingEdgeTriggeredDFlipFlop risingedgetriggereddflipflop_9 (
    .D(I[1]), .clk(clk), .Q(Q[1]), .W_Enable(W_Enable), .reset(reset));
  RisingEdgeTriggeredDFlipFlop risingedgetriggereddflipflop_10 (
    .D(I[0]), .clk(clk), .Q(Q[0]), .W_Enable(W_Enable), .reset(reset));

  // Notes on the sheet:
  //   Q: pull=down
  //   reset: pull=down
  //   clk: pull=down
  //   W_Enable: pull=down
  //   I: pull=down
endmodule
