// Logisim project 20BitRegister.circ as structural Verilog: 1 circuit, main circuit 20BitRegister
module _20BitRegister (
  input  [19:0] I,
  input  clk,
  input  W_Enable,
  input  reset,
  output [19:0] Q
);

  RisingEdgeTriggeredDFlipFlop risingedgetriggereddflipflop_1 (
    .D(I[19]), .clk(clk), .Q(Q[19]), .W_Enable(W_Enable), .reset(reset));
  RisingEdgeTriggeredDFlipFlop risingedgetriggereddflipflop_2 (
    .D(I[18]), .clk(clk), .Q(Q[18]), .W_Enable(W_Enable), .reset(reset));
  RisingEdgeTriggeredDFlipFlop risingedgetriggereddflipflop_3 (
    .D(I[17]), .clk(clk), .Q(Q[17]), .W_Enable(W_Enable), .reset(reset));
  RisingEdgeTriggeredDFlipFlop risingedgetriggereddflipflop_4 (
    .D(I[16]), .clk(clk), .Q(Q[16]), .W_Enable(W_Enable), .reset(reset));
  RisingEdgeTriggeredDFlipFlop risingedgetriggereddflipflop_5 (
    .D(I[15]), .clk(clk), .Q(Q[15]), .W_Enable(W_Enable), .reset(reset));
  RisingEdgeTriggeredDFlipFlop risingedgetriggereddflipflop_6 (
    .D(I[14]), .clk(clk), .Q(Q[14]), .W_Enable(W_Enable), .reset(reset));
  RisingEdgeTriggeredDFlipFlop risingedgetriggereddflipflop_7 (
    .D(I[13]), .clk(clk), .Q(Q[13]), .W_Enable(W_Enable), .reset(reset));
  RisingEdgeTriggeredDFlipFlop risingedgetriggereddflipflop_8 (
    .D(I[12]), .clk(clk), .Q(Q[12]), .W_Enable(W_Enable), .reset(reset));
  RisingEdgeTriggeredDFlipFlop risingedgetriggereddflipflop_9 (
    .D(I[11]), .clk(clk), .Q(Q[11]), .W_Enable(W_Enable), .reset(reset));
  RisingEdgeTriggeredDFlipFlop risingedgetriggereddflipflop_10 (
    .D(I[10]), .clk(clk), .Q(Q[10]), .W_Enable(W_Enable), .reset(reset));
  RisingEdgeTriggeredDFlipFlop risingedgetriggereddflipflop_11 (
    .D(I[9]), .clk(clk), .Q(Q[9]), .W_Enable(W_Enable), .reset(reset));
  RisingEdgeTriggeredDFlipFlop risingedgetriggereddflipflop_12 (
    .D(I[8]), .clk(clk), .Q(Q[8]), .W_Enable(W_Enable), .reset(reset));
  RisingEdgeTriggeredDFlipFlop risingedgetriggereddflipflop_13 (
    .D(I[7]), .clk(clk), .Q(Q[7]), .W_Enable(W_Enable), .reset(reset));
  RisingEdgeTriggeredDFlipFlop risingedgetriggereddflipflop_14 (
    .D(I[6]), .clk(clk), .Q(Q[6]), .W_Enable(W_Enable), .reset(reset));
  RisingEdgeTriggeredDFlipFlop risingedgetriggereddflipflop_15 (
    .D(I[5]), .clk(clk), .Q(Q[5]), .W_Enable(W_Enable), .reset(reset));
  RisingEdgeTriggeredDFlipFlop risingedgetriggereddflipflop_16 (
    .D(I[4]), .clk(clk), .Q(Q[4]), .W_Enable(W_Enable), .reset(reset));
  RisingEdgeTriggeredDFlipFlop risingedgetriggereddflipflop_17 (
    .D(I[3]), .clk(clk), .Q(Q[3]), .W_Enable(W_Enable), .reset(reset));
  RisingEdgeTriggeredDFlipFlop risingedgetriggereddflipflop_18 (
    .D(I[2]), .clk(clk), .Q(Q[2]), .W_Enable(W_Enable), .reset(reset));
  RisingEdgeTriggeredDFlipFlop risingedgetriggereddflipflop_19 (
    .D(I[1]), .clk(clk), .Q(Q[1]), .W_Enable(W_Enable), .reset(reset));
  RisingEdgeTriggeredDFlipFlop risingedgetriggereddflipflop_20 (
    .D(I[0]), .clk(clk), .Q(Q[0]), .W_Enable(W_Enable), .reset(reset));

  // Notes on the sheet:
  //   I: pull=down
  //   clk: pull=down
  //   Q: pull=down
  //   reset: pull=down
  //   W_Enable: pull=down
endmodule
