// Logisim project 20BitSubtractor.circ as structural Verilog: 1 circuit, main circuit 20BitSubtractor
module _20BitSubtractor (
  input  [19:0] N0,
  input  [19:0] N1,
  output O,
  output [19:0] D
);

  wire fullsubtractor_2_b_out, fullsubtractor_3_b_out, fullsubtractor_4_b_out, fullsubtractor_5_b_out,
       fullsubtractor_6_b_out, fullsubtractor_7_b_out, fullsubtractor_8_b_out, fullsubtractor_9_b_out,
       fullsubtractor_10_b_out, fullsubtractor_11_b_out, fullsubtractor_12_b_out, fullsubtractor_13_b_out,
       fullsubtractor_14_b_out, fullsubtractor_15_b_out, fullsubtractor_16_b_out, fullsubtractor_17_b_out,
       fullsubtractor_18_b_out, fullsubtractor_19_b_out, halfsubtractor_1_b;

  HalfSubtractor halfsubtractor_1 (.N0(N0[0]), .N1(N1[0]), .D(D[0]), .B(halfsubtractor_1_b));
  FullSubtractor fullsubtractor_1 (.I0(N0[19]), .I1(N1[19]), .B_in(fullsubtractor_3_b_out), .D(D[19]), .B_out(O));
  FullSubtractor fullsubtractor_2 (
    .I0(N0[1]), .I1(N1[1]), .B_in(halfsubtractor_1_b), .D(D[1]), .B_out(fullsubtractor_2_b_out));
  FullSubtractor fullsubtractor_3 (
    .I0(N0[18]), .I1(N1[18]), .B_in(fullsubtractor_5_b_out), .D(D[18]), .B_out(fullsubtractor_3_b_out));
  FullSubtractor fullsubtractor_4 (
    .I0(N0[2]), .I1(N1[2]), .B_in(fullsubtractor_2_b_out), .D(D[2]), .B_out(fullsubtractor_4_b_out));
  FullSubtractor fullsubtractor_5 (
    .I0(N0[17]), .I1(N1[17]), .B_in(fullsubtractor_7_b_out), .D(D[17]), .B_out(fullsubtractor_5_b_out));
  FullSubtractor fullsubtractor_6 (
    .I0(N0[3]), .I1(N1[3]), .B_in(fullsubtractor_4_b_out), .D(D[3]), .B_out(fullsubtractor_6_b_out));
  FullSubtractor fullsubtractor_7 (
    .I0(N0[16]), .I1(N1[16]), .B_in(fullsubtractor_10_b_out), .D(D[16]), .B_out(fullsubtractor_7_b_out));
  FullSubtractor fullsubtractor_8 (
    .I0(N0[5]), .I1(N1[5]), .B_in(fullsubtractor_9_b_out), .D(D[5]), .B_out(fullsubtractor_8_b_out));
  FullSubtractor fullsubtractor_9 (
    .I0(N0[4]), .I1(N1[4]), .B_in(fullsubtractor_6_b_out), .D(D[4]), .B_out(fullsubtractor_9_b_out));
  FullSubtractor fullsubtractor_10 (
    .I0(N0[15]), .I1(N1[15]), .B_in(fullsubtractor_11_b_out), .D(D[15]), .B_out(fullsubtractor_10_b_out));
  FullSubtractor fullsubtractor_11 (
    .I0(N0[14]), .I1(N1[14]), .B_in(fullsubtractor_13_b_out), .D(D[14]), .B_out(fullsubtractor_11_b_out));
  FullSubtractor fullsubtractor_12 (
    .I0(N0[6]), .I1(N1[6]), .B_in(fullsubtractor_8_b_out), .D(D[6]), .B_out(fullsubtractor_12_b_out));
  FullSubtractor fullsubtractor_13 (
    .I0(N0[13]), .I1(N1[13]), .B_in(fullsubtractor_15_b_out), .D(D[13]), .B_out(fullsubtractor_13_b_out));
  FullSubtractor fullsubtractor_14 (
    .I0(N0[7]), .I1(N1[7]), .B_in(fullsubtractor_12_b_out), .D(D[7]), .B_out(fullsubtractor_14_b_out));
  FullSubtractor fullsubtractor_15 (
    .I0(N0[12]), .I1(N1[12]), .B_in(fullsubtractor_17_b_out), .D(D[12]), .B_out(fullsubtractor_15_b_out));
  FullSubtractor fullsubtractor_16 (
    .I0(N0[8]), .I1(N1[8]), .B_in(fullsubtractor_14_b_out), .D(D[8]), .B_out(fullsubtractor_16_b_out));
  FullSubtractor fullsubtractor_17 (
    .I0(N0[11]), .I1(N1[11]), .B_in(fullsubtractor_19_b_out), .D(D[11]), .B_out(fullsubtractor_17_b_out));
  FullSubtractor fullsubtractor_18 (
    .I0(N0[9]), .I1(N1[9]), .B_in(fullsubtractor_16_b_out), .D(D[9]), .B_out(fullsubtractor_18_b_out));
  FullSubtractor fullsubtractor_19 (
    .I0(N0[10]), .I1(N1[10]), .B_in(fullsubtractor_18_b_out), .D(D[10]), .B_out(fullsubtractor_19_b_out));

  // Notes on the sheet:
  //   N1: pull=down
  //   O: pull=down
  //   N0: pull=down
  //   D: pull=down
endmodule
