// Logisim project 10BitDecrementer.circ as structural Verilog: 1 circuit, main circuit 10BitDecrementer
module _10BitDecrementer (
  input  [9:0] I,
  output [9:0] S,
  output Overflow
);

  wire halfsubtractor_1_b_out, halfsubtractor_2_b_out, halfsubtractor_3_b_out, halfsubtractor_4_b_out,
       halfsubtractor_5_b_out, halfsubtractor_6_b_out, halfsubtractor_7_b_out, halfsubtractor_8_b_out,
       halfsubtractor_9_b_out;

  HalfSubtractor halfsubtractor_1 (.I0(I[0]), .I1(1'b1), .D(S[0]), .B_out(halfsubtractor_1_b_out));
  HalfSubtractor halfsubtractor_2 (.I0(I[1]), .I1(halfsubtractor_1_b_out), .D(S[1]), .B_out(halfsubtractor_2_b_out));
  HalfSubtractor halfsubtractor_3 (.I0(I[2]), .I1(halfsubtractor_2_b_out), .D(S[2]), .B_out(halfsubtractor_3_b_out));
  HalfSubtractor halfsubtractor_4 (.I0(I[3]), .I1(halfsubtractor_3_b_out), .D(S[3]), .B_out(halfsubtractor_4_b_out));
  HalfSubtractor halfsubtractor_5 (.I0(I[4]), .I1(halfsubtractor_4_b_out), .D(S[4]), .B_out(halfsubtractor_5_b_out));
  HalfSubtractor halfsubtractor_6 (.I0(I[5]), .I1(halfsubtractor_5_b_out), .D(S[5]), .B_out(halfsubtractor_6_b_out));
  HalfSubtractor halfsubtractor_7 (.I0(I[7]), .I1(halfsubtractor_8_b_out), .D(S[7]), .B_out(halfsubtractor_7_b_out));
  HalfSubtractor halfsubtractor_8 (.I0(I[6]), .I1(halfsubtractor_6_b_out), .D(S[6]), .B_out(halfsubtractor_8_b_out));
  HalfSubtractor halfsubtractor_9 (.I0(I[8]), .I1(halfsubtractor_7_b_out), .D(S[8]), .B_out(halfsubtractor_9_b_out));
  HalfSubtractor halfsubtractor_10 (.I0(I[9]), .I1(halfsubtractor_9_b_out), .D(S[9]), .B_out(Overflow));

  // Notes on the sheet:
  //   Overflow: pull=down
  //   I: pull=down
  //   S: pull=down
endmodule
