// Logisim project FullSubtractor.circ as structural Verilog: 1 circuit, main circuit FullSubtractor
module FullSubtractor (
  input  N0,
  input  N1,
  input  Bin,
  output D,
  output Bout
);

  wire halfsubtractor_1_b, halfsubtractor_1_d, halfsubtractor_2_b;

  HalfSubtractor halfsubtractor_1 (.N0(N0), .N1(N1), .D(halfsubtractor_1_d), .B(halfsubtractor_1_b));
  HalfSubtractor halfsubtractor_2 (.N0(halfsubtractor_1_d), .N1(Bin), .D(D), .B(halfsubtractor_2_b));
  or or_1 (Bout, halfsubtractor_2_b, halfsubtractor_1_b);

  // Notes on the sheet:
  //   N1: pull=down
  //   N0: pull=down
  //   Bin: pull=down
  //   Bout: pull=down
  //   D: pull=down
endmodule
