// Logisim project HalfSubtractor.circ as structural Verilog: 1 circuit, main circuit HalfSubtractor
module HalfSubtractor (
  input  I0,
  input  I1,
  output D,
  output B_out
);

  wire not_1_out;

  xor xor_1 (D, I0, I1);
  and and_1 (B_out, I1, not_1_out);
  not not_1 (not_1_out, I0);

  // Notes on the sheet:
  //   I1: pull=down
  //   D: pull=down
  //   B_out: pull=down
  //   I0: pull=down
endmodule
