// Logisim project circuits.circ as structural Verilog: 4 circuits, main circuit main
module main (
  input  [19:0] in_1,
  input  [19:0] in_2,
  output [19:0] out_3,
  output out_4
);

  Adder adder_1 (.N0(in_1), .N1(in_2), .S(out_3), .O(out_4));
endmodule

module Half_Adder (
  input  A,
  input  B,
  output S,
  output C
);

  xor xor_1 (S, A, B);
  and and_1 (C, A, B);
endmodule

module Full_Adder (
  input  C_in,
  input  A,
  input  B,
  output S,
  output C_out
);

  wire Half_Adder_2_c, Half_Adder_c, Half_Adder_s;

  Half_Adder Half_Adder (.A(A), .B(B), .S(Half_Adder_s), .C(Half_Adder_c));
  Half_Adder Half_Adder_2 (.A(C_in), .B(Half_Adder_s), .S(S), .C(Half_Adder_2_c));
  or or_1 (C_out, Half_Adder_2_c, Half_Adder_c);
endmodule

module Adder (
  input  [19:0] N0,
  input  [19:0] N1,
  output [19:0] S,
  output O
);

  wire full_adder_1_c_out, full_adder_2_c_out, full_adder_3_c_out, full_adder_4_c_out, full_adder_5_c_out,
       full_adder_6_c_out, full_adder_7_c_out, full_adder_8_c_out, full_adder_9_c_out, full_adder_10_c_out,
       full_adder_11_c_out, full_adder_12_c_out, full_adder_13_c_out, full_adder_14_c_out,
       full_adder_15_c_out, full_adder_16_c_out, full_adder_17_c_out, full_adder_18_c_out,
       full_adder_19_c_out;

  Full_Adder full_adder_1 (.C_in(1'b0), .A(N0[0]), .B(N1[0]), .S(S[0]), .C_out(full_adder_1_c_out));
  Full_Adder full_adder_2 (.C_in(full_adder_1_c_out), .A(N0[1]), .B(N1[1]), .S(S[1]), .C_out(full_adder_2_c_out));
  Full_Adder full_adder_3 (.C_in(full_adder_2_c_out), .A(N0[2]), .B(N1[2]), .S(S[2]), .C_out(full_adder_3_c_out));
  Full_Adder full_adder_4 (.C_in(full_adder_3_c_out), .A(N0[3]), .B(N1[3]), .S(S[3]), .C_out(full_adder_4_c_out));
  Full_Adder full_adder_5 (.C_in(full_adder_4_c_out), .A(N0[4]), .B(N1[4]), .S(S[4]), .C_out(full_adder_5_c_out));
  Full_Adder full_adder_6 (.C_in(full_adder_5_c_out), .A(N0[5]), .B(N1[5]), .S(S[5]), .C_out(full_adder_6_c_out));
  Full_Adder full_adder_7 (.C_in(full_adder_6_c_out), .A(N0[6]), .B(N1[6]), .S(S[6]), .C_out(full_adder_7_c_out));
  Full_Adder full_adder_8 (.C_in(full_adder_7_c_out), .A(N0[7]), .B(N1[7]), .S(S[7]), .C_out(full_adder_8_c_out));
  Full_Adder full_adder_9 (.C_in(full_adder_8_c_out), .A(N0[8]), .B(N1[8]), .S(S[8]), .C_out(full_adder_9_c_out));
  Full_Adder full_adder_10 (.C_in(full_adder_9_c_out), .A(N0[9]), .B(N1[9]), .S(S[9]), .C_out(full_adder_10_c_out));
  Full_Adder full_adder_11 (.C_in(full_adder_10_c_out), .A(N0[10]), .B(N1[10]), .S(S[10]), .C_out(full_adder_11_c_out));
  Full_Adder full_adder_12 (.C_in(full_adder_11_c_out), .A(N0[11]), .B(N1[11]), .S(S[11]), .C_out(full_adder_12_c_out));
  Full_Adder full_adder_13 (.C_in(full_adder_12_c_out), .A(N0[12]), .B(N1[12]), .S(S[12]), .C_out(full_adder_13_c_out));
  Full_Adder full_adder_14 (.C_in(full_adder_13_c_out), .A(N0[13]), .B(N1[13]), .S(S[13]), .C_out(full_adder_14_c_out));
  Full_Adder full_adder_15 (.C_in(full_adder_14_c_out), .A(N0[14]), .B(N1[14]), .S(S[14]), .C_out(full_adder_15_c_out));
  Full_Adder full_adder_16 (.C_in(full_adder_15_c_out), .A(N0[15]), .B(N1[15]), .S(S[15]), .C_out(full_adder_16_c_out));
  Full_Adder full_adder_17 (.C_in(full_adder_16_c_out), .A(N0[16]), .B(N1[16]), .S(S[16]), .C_out(full_adder_17_c_out));
  Full_Adder full_adder_18 (.C_in(full_adder_17_c_out), .A(N0[17]), .B(N1[17]), .S(S[17]), .C_out(full_adder_18_c_out));
  Full_Adder full_adder_19 (.C_in(full_adder_18_c_out), .A(N0[18]), .B(N1[18]), .S(S[18]), .C_out(full_adder_19_c_out));
  Full_Adder full_adder_20 (.C_in(full_adder_19_c_out), .A(N0[19]), .B(N1[19]), .S(S[19]), .C_out(O));
endmodule
